# Fritzing sketch SchemaLogicoArduino (saved by Fritzing 0.9.3b)
breadboards: 2

parts:
  U1 = 74LVC138AD [package=so016]
  Componente2 = Arduino Uno (Rev3) - ICSP
  C1 = Capacitor Polarized [package=panasonic_d]
  M1 = Stepper Motor - Bipolar
  U2 = 74LVC138AD [package=so016]
  C2 = Capacitor Polarized [package=panasonic_d]
  M2 = Stepper Motor - Bipolar

nets:
  N1: U1.A0, Componente2.D8
  N2: U1._E2, U1.E3
  N3: U1._Y7, Componente2.D6_PWM
  N4: U1.GND, Componente2.D7
  N5: U1._Y6, Componente2.GND, U2._Y6
  N6: U1._Y5, Componente2.VIN, U2._Y5
  N7: U1._Y4, M1.D
  N8: U1._Y3, M1.B
  N9: U1._Y2, M1.C
  N10: U1._Y1, M1.A
  N11: U1._Y0, C1.+, U2._Y0, C2.+
  VCC: U1.VCC, C1.-, U2.VCC, C2.-
  N12: Componente2.D9_PWM, U2.A0
  N13: Componente2.D4, U2._Y7
  N14: Componente2.D5_PWM, U2.GND
  N15: U2._E2, U2.E3
  N16: U2._Y4, M2.D
  N17: U2._Y3, M2.B
  N18: U2._Y2, M2.C
  N19: U2._Y1, M2.A

notes:
  alimentatore 12V
